// Logisim project スロットデコーダ.circ as structural Verilog: 1 circuit, main circuit main
module main (
  input  SLT0,
  input  SLT3,
  input  A15,
  output ROMCE,
  output A16,
  output RAMCE
);

  wire not_2_out, or_2_out;

  or or_1 (ROMCE, A15, SLT0);
  not not_1 (A16, SLT3);
  not not_2 (not_2_out, A15);
  or or_2 (or_2_out, SLT0, not_2_out);
  and and_1 (RAMCE, SLT3, or_2_out);
endmodule
